# Fritzing sketch Lesson3_LED (saved by Fritzing 1.0.1rc)
breadboards: 1

parts:
  Pico/Pico2_Mod_1 = Raspberry Pi Pico or Pico 2
  R1 = Resistor [tolerance=±5% resistance=220 package="0805 [SMD]"]
  LED1 = LEDs [package=led10mm]

nets:
  N1: Pico/Pico2_Mod_1.pin_5, Pico/Pico2_Mod_1.pin_12, Pico/Pico2_Mod_1.pin_13, Pico/Pico2_Mod_1.pin_14, Pico/Pico2_Mod_1.pin_17, Pico/Pico2_Mod_1.pin_18, Pico/Pico2_Mod_1.pin_23, Pico/Pico2_Mod_1.pin_28, Pico/Pico2_Mod_1.pin_33, Pico/Pico2_Mod_1.pin_38
  N2: Pico/Pico2_Mod_1.pin_29, Pico/Pico2_Mod_1.pin_37, LED1.C
  N3: R1.Pin_1, LED1.A

custom parts:
  Raspberry Pi Pico or Pico 2: Raspberry Pi Pico and Pico 2. Based around the RP2040 and RP2350 microcontrollers respectively, Picos are low cost microcontroller device bringing Raspberry Pi quality, cost, and easy of use to the microcontroller space. Jan 2021, Split part in to two versions: tht (this one) and SMD. This one will drill holes for a .1 in header in pcb to allow plugging in the module as well as providing pads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
