# Fritzing sketch Lesson5_Button (saved by Fritzing 1.0.1rc)
breadboards: 1

parts:
  Pico/Pico2_Mod_1 = Raspberry Pi Pico or Pico 2
  LED2 = LEDs [package=led10mm]
  R1 = Resistor [tolerance=±5% resistance=220 package="2010 [SMD]"]
  J1 = Piezo Speaker
  S1 = Pushbutton [package="[THT]"]

nets:
  N1: Pico/Pico2_Mod_1.pin_1, Pico/Pico2_Mod_1.pin_3, Pico/Pico2_Mod_1.pin_13, Pico/Pico2_Mod_1.pin_23, Pico/Pico2_Mod_1.pin_28, Pico/Pico2_Mod_1.pin_33, Pico/Pico2_Mod_1.pin_38, Pico/Pico2_Mod_1.pin_42
  N2: Pico/Pico2_Mod_1.pin_11, Pico/Pico2_Mod_1.pin_14, Pico/Pico2_Mod_1.pin_29, LED2.C, J1.pin1, S1.Pin_1, S1.Pin_2
  N3: Pico/Pico2_Mod_1.pin_15, LED2.A, R1.Pin_1
  N4: S1.Pin_3, S1.Pin_4

custom parts:
  Raspberry Pi Pico or Pico 2: Raspberry Pi Pico and Pico 2. Based around the RP2040 and RP2350 microcontrollers respectively, Picos are low cost microcontroller device bringing Raspberry Pi quality, cost, and easy of use to the microcontroller space. Jan 2021, Split part in to two versions: tht (this one) and SMD. This one will drill holes for a .1 in header in pcb to allow plugging in the module as well as providing pads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
